// Logisim project alu.circ as structural Verilog: 1 circuit, main circuit alu
module alu (
  input  [31:0] A,
  input  [31:0] B,
  input  [3:0] ALUSel,
  output [31:0] ALUResult
);

  wire comparator_1_lt;
  wire [4:0] bitselector_1_out, bitselector_2_out, bitselector_3_out;
  wire [31:0] adder_1_out, and_1_out, bit_extender_5_out, or_1_out, shifter_1_out, shifter_2_out,
       shifter_3_out, subtractor_1_out, xor_1_out;
  wire [63:0] bit_extender_1_out, bit_extender_2_out, bit_extender_3_out, bit_extender_4_out,
       multiplier_1_out, multiplier_2_out;

  Adder #(.width(32)) adder_1 (.a(A), .b(B), .out(adder_1_out));  // open: cin, cout
  BitSelector #(.group(5), .width(32)) bitselector_1 (.in(B), .out(bitselector_1_out), .sel(3'b000));
  Comparator #(.width(32)) comparator_1 (.a(A), .b(B), .lt(comparator_1_lt));  // open: gt, eq
  BitSelector #(.group(5), .width(32)) bitselector_2 (.in(B), .out(bitselector_2_out), .sel(3'b000));
  assign or_1_out = A | B;  // OR_Gate or_1, 32 bits wide
  assign and_1_out = A & B;  // AND_Gate and_1, 32 bits wide
  assign bit_extender_1_out = {{32{A[31]}}, A};  // Bit_Extender bit_extender_1
  assign bit_extender_2_out = {{32{B[31]}}, B};  // Bit_Extender bit_extender_2
  assign bit_extender_3_out = {{32{1'b0}}, A};  // Bit_Extender bit_extender_3
  assign bit_extender_4_out = {{32{1'b0}}, B};  // Bit_Extender bit_extender_4
  BitSelector #(.group(5), .width(32)) bitselector_3 (.in(B), .out(bitselector_3_out), .sel(3'b000));
  assign bit_extender_5_out = {{31{1'b0}}, comparator_1_lt};  // Bit_Extender bit_extender_5
  assign xor_1_out = A ^ B;  // XOR_Gate xor_1, 32 bits wide
  Shifter #(.shift("lr"), .width(32)) shifter_1 (.in(A), .\dist (bitselector_2_out), .out(shifter_1_out));
  Multiplier #(.mode("twosComplement"), .width(64)) multiplier_1 (
    .a(bit_extender_1_out), .b(bit_extender_2_out), .out(multiplier_1_out));  // open: cin, cout
  Multiplier #(.width(64)) multiplier_2 (
    .a(bit_extender_3_out), .b(bit_extender_4_out), .out(multiplier_2_out));  // open: cin, cout
  Subtractor #(.width(32)) subtractor_1 (.a(A), .b(B), .out(subtractor_1_out));  // open: bin, bout
  Shifter #(.width(32)) shifter_2 (.in(A), .\dist (bitselector_1_out), .out(shifter_2_out));
  Shifter #(.shift("ar"), .width(32)) shifter_3 (.in(A), .\dist (bitselector_3_out), .out(shifter_3_out));
  Multiplexer #(.select(4), .width(32)) multiplexer_1 (
    .in0(adder_1_out), .in1(shifter_2_out), .in2(bit_extender_5_out), .in4(xor_1_out), .in5(shifter_1_out),
    .in6(or_1_out), .in7(and_1_out), .in8(multiplier_1_out[31:0]), .in9(multiplier_1_out[63:32]),
    .in11(multiplier_2_out[63:32]), .in12(subtractor_1_out), .in13(shifter_3_out), .in15(B), .out(ALUResult),
    .sel(ALUSel));  // open: in3, in10, in14

  // Notes on the sheet:
  //   INPUTS to your circuit
  //   DON'T CHANGE THE LOCATIONS OF THE INPUTS AND OUTPUTS!
  //   OUTPUT from your circuit
endmodule
