// Logisim project control-logic.circ as structural Verilog: 1 circuit, main circuit control_logic
module control_logic (
  input  [31:0] Instruction,
  input  BrEq,
  input  BrLt,
  output PCSel,
  output RegWEn,
  output [2:0] ImmSel,
  output BrUn,
  output ASel,
  output BSel,
  output [3:0] ALUSel,
  output MemWEn,
  output [1:0] WBSel
);

  wire and_22_out, and_23_out, and_24_out, and_31_out, and_32_out, and_33_out, comparator_10_eq,
       comparator_11_eq, comparator_12_eq, comparator_13_eq, comparator_14_eq, comparator_15_eq,
       comparator_16_eq, comparator_17_eq, comparator_18_eq, comparator_19_eq, comparator_20_eq,
       comparator_21_eq, comparator_22_eq, comparator_23_eq, comparator_24_eq, comparator_25_eq,
       comparator_26_eq, comparator_27_eq, comparator_28_eq, comparator_29_eq, comparator_30_eq,
       comparator_31_eq, comparator_32_eq, comparator_33_eq, comparator_34_eq, comparator_35_eq,
       comparator_36_eq, comparator_37_eq, comparator_38_eq, comparator_39_eq, comparator_40_eq,
       comparator_41_eq, comparator_42_eq, comparator_43_eq, comparator_44_eq, comparator_45_eq,
       comparator_46_eq, comparator_47_eq, comparator_48_eq, comparator_49_eq, comparator_50_eq,
       comparator_51_eq, comparator_52_eq, comparator_53_eq, comparator_54_eq, isAdd, isAddi, isAnd, isAndi,
       isAuipc, isB, isBeq, isBge, isBgeu, isBlt, isBltu, isBne, isI, isJ, isJr, isLb, isLd, isLh, isLui,
       isLw, isMul, isMulh, isMulhu, isOr, isOri, isR, isS, isSb, isSh, isSll, isSlli, isSlt, isSlti, isSra,
       isSrai, isSri, isSrl, isSrli, isSub, isSw, isXor, isXori, not_1_out, not_2_out, not_3_out, or_1_out,
       priority_encoder_1_gs, priority_encoder_2_gs, priority_encoder_3_gs, priority_encoder_4_gs,
       priority_encoder_5_gs;
  wire [1:0] priority_encoder_2_out;
  wire [2:0] priority_encoder_1_out, priority_encoder_3_out, priority_encoder_4_out;
  wire [3:0] priority_encoder_5_out;
  wire [5:0] and_40_out, and_41_out, and_42_out, and_43_out, and_44_out, BAddr, bit_extender_1_out,
       bit_extender_2_out, bit_extender_3_out, bit_extender_4_out, bit_extender_5_out, IAddr, JUAddr,
       MemAddr, RAddr, RomAddr;
  wire [15:14] rom_1_data;

  Comparator #(.width(7)) comparator_1 (.a(7'b0010011), .b(Instruction[6:0]), .eq(isI));  // open: gt, lt
  Comparator #(.width(7)) comparator_2 (.a(7'b0110011), .b(Instruction[6:0]), .eq(isR));  // open: gt, lt
  Comparator #(.width(7)) comparator_3 (.a(7'b1100011), .b(Instruction[6:0]), .eq(isB));  // open: gt, lt
  Comparator #(.width(7)) comparator_4 (.a(7'b0000011), .b(Instruction[6:0]), .eq(isLd));  // open: gt, lt
  Comparator #(.width(7)) comparator_5 (.a(7'b0100011), .b(Instruction[6:0]), .eq(isS));  // open: gt, lt
  Comparator #(.width(7)) comparator_6 (.a(7'b1101111), .b(Instruction[6:0]), .eq(isJ));  // open: gt, lt
  Comparator #(.width(7)) comparator_7 (.a(7'b1100111), .b(Instruction[6:0]), .eq(isJr));  // open: gt, lt
  Comparator #(.width(7)) comparator_8 (.a(7'b0010111), .b(Instruction[6:0]), .eq(isAuipc));  // open: gt, lt
  Comparator #(.width(7)) comparator_9 (.a(7'b0110111), .b(Instruction[6:0]), .eq(isLui));  // open: gt, lt
  ROM #(.addrWidth(6), .dataWidth(16)) rom_1 (
    .addr(RomAddr), .data({rom_1_data, WBSel, MemWEn, ALUSel, BSel, ASel, BrUn, ImmSel, RegWEn}));
  Comparator #(.width(3)) comparator_10 (.a(3'b000), .b(Instruction[14:12]), .eq(comparator_10_eq));  // open: gt, lt
  Comparator #(.width(3)) comparator_11 (.a(3'b111), .b(Instruction[14:12]), .eq(comparator_11_eq));  // open: gt, lt
  Comparator #(.width(3)) comparator_12 (.a(3'b110), .b(Instruction[14:12]), .eq(comparator_12_eq));  // open: gt, lt
  Comparator #(.width(3)) comparator_13 (.a(3'b100), .b(Instruction[14:12]), .eq(comparator_13_eq));  // open: gt, lt
  Comparator #(.width(3)) comparator_14 (.a(3'b001), .b(Instruction[14:12]), .eq(comparator_14_eq));  // open: gt, lt
  Comparator #(.width(3)) comparator_15 (.a(3'b101), .b(Instruction[14:12]), .eq(comparator_15_eq));  // open: gt, lt
  Comparator #(.width(3)) comparator_16 (.a(3'b010), .b(Instruction[14:12]), .eq(comparator_16_eq));  // open: gt, lt
  Comparator #(.width(7)) comparator_17 (.a({7{1'b0}}), .b(Instruction[31:25]), .eq(comparator_17_eq));  // open: gt, lt
  Comparator #(.width(7)) comparator_18 (
    .a(7'b0100000), .b(Instruction[31:25]), .eq(comparator_18_eq));  // open: gt, lt
  and and_1 (isAddi, isI, comparator_10_eq);
  and and_2 (isAndi, isI, comparator_11_eq);
  and and_3 (isOri, isI, comparator_12_eq);
  and and_4 (isXori, isI, comparator_13_eq);
  and and_5 (isSlli, isI, comparator_14_eq);
  and and_6 (isSri, isI, comparator_15_eq);
  and and_7 (isSlti, isI, comparator_16_eq);
  and and_8 (isSrli, isSri, comparator_17_eq);
  and and_9 (isSrai, isSri, comparator_18_eq);
  Comparator #(.width(7)) comparator_19 (.a({7{1'b0}}), .b(Instruction[31:25]), .eq(comparator_19_eq));  // open: gt, lt
  Comparator #(.width(3)) comparator_20 (.a(3'b000), .b(Instruction[14:12]), .eq(comparator_20_eq));  // open: gt, lt
  Comparator #(.width(7)) comparator_21 (
    .a(7'b0100000), .b(Instruction[31:25]), .eq(comparator_21_eq));  // open: gt, lt
  Comparator #(.width(3)) comparator_22 (.a(3'b000), .b(Instruction[14:12]), .eq(comparator_22_eq));  // open: gt, lt
  Comparator #(.width(7)) comparator_23 (.a({7{1'b0}}), .b(Instruction[31:25]), .eq(comparator_23_eq));  // open: gt, lt
  Comparator #(.width(3)) comparator_24 (.a(3'b111), .b(Instruction[14:12]), .eq(comparator_24_eq));  // open: gt, lt
  Comparator #(.width(7)) comparator_25 (.a({7{1'b0}}), .b(Instruction[31:25]), .eq(comparator_25_eq));  // open: gt, lt
  Comparator #(.width(3)) comparator_26 (.a(3'b110), .b(Instruction[14:12]), .eq(comparator_26_eq));  // open: gt, lt
  Comparator #(.width(7)) comparator_27 (.a({7{1'b0}}), .b(Instruction[31:25]), .eq(comparator_27_eq));  // open: gt, lt
  Comparator #(.width(3)) comparator_28 (.a(3'b100), .b(Instruction[14:12]), .eq(comparator_28_eq));  // open: gt, lt
  Comparator #(.width(7)) comparator_29 (.a({7{1'b0}}), .b(Instruction[31:25]), .eq(comparator_29_eq));  // open: gt, lt
  Comparator #(.width(3)) comparator_30 (.a(3'b001), .b(Instruction[14:12]), .eq(comparator_30_eq));  // open: gt, lt
  Comparator #(.width(7)) comparator_31 (.a({7{1'b0}}), .b(Instruction[31:25]), .eq(comparator_31_eq));  // open: gt, lt
  Comparator #(.width(3)) comparator_32 (.a(3'b101), .b(Instruction[14:12]), .eq(comparator_32_eq));  // open: gt, lt
  Comparator #(.width(7)) comparator_33 (
    .a(7'b0100000), .b(Instruction[31:25]), .eq(comparator_33_eq));  // open: gt, lt
  Comparator #(.width(3)) comparator_34 (.a(3'b101), .b(Instruction[14:12]), .eq(comparator_34_eq));  // open: gt, lt
  Comparator #(.width(7)) comparator_35 (.a({7{1'b0}}), .b(Instruction[31:25]), .eq(comparator_35_eq));  // open: gt, lt
  Comparator #(.width(3)) comparator_36 (.a(3'b010), .b(Instruction[14:12]), .eq(comparator_36_eq));  // open: gt, lt
  Comparator #(.width(7)) comparator_37 (
    .a(7'b0000001), .b(Instruction[31:25]), .eq(comparator_37_eq));  // open: gt, lt
  Comparator #(.width(3)) comparator_38 (.a(3'b000), .b(Instruction[14:12]), .eq(comparator_38_eq));  // open: gt, lt
  Comparator #(.width(7)) comparator_39 (
    .a(7'b0000001), .b(Instruction[31:25]), .eq(comparator_39_eq));  // open: gt, lt
  Comparator #(.width(3)) comparator_40 (.a(3'b001), .b(Instruction[14:12]), .eq(comparator_40_eq));  // open: gt, lt
  Comparator #(.width(7)) comparator_41 (
    .a(7'b0000001), .b(Instruction[31:25]), .eq(comparator_41_eq));  // open: gt, lt
  Comparator #(.width(3)) comparator_42 (.a(3'b011), .b(Instruction[14:12]), .eq(comparator_42_eq));  // open: gt, lt
  and and_10 (isAdd, isR, comparator_19_eq, comparator_20_eq);
  and and_11 (isSub, isR, comparator_21_eq, comparator_22_eq);
  and and_12 (isAnd, isR, comparator_23_eq, comparator_24_eq);
  and and_13 (isOr, isR, comparator_25_eq, comparator_26_eq);
  and and_14 (isXor, isR, comparator_27_eq, comparator_28_eq);
  and and_15 (isSll, isR, comparator_29_eq, comparator_30_eq);
  and and_16 (isSrl, isR, comparator_31_eq, comparator_32_eq);
  and and_17 (isSra, isR, comparator_33_eq, comparator_34_eq);
  and and_18 (isSlt, isR, comparator_35_eq, comparator_36_eq);
  and and_19 (isMul, isR, comparator_37_eq, comparator_38_eq);
  and and_20 (isMulh, isR, comparator_39_eq, comparator_40_eq);
  and and_21 (isMulhu, isR, comparator_41_eq, comparator_42_eq);
  Comparator #(.width(3)) comparator_43 (.a(3'b000), .b(Instruction[14:12]), .eq(comparator_43_eq));  // open: gt, lt
  Comparator #(.width(3)) comparator_44 (.a(3'b101), .b(Instruction[14:12]), .eq(comparator_44_eq));  // open: gt, lt
  Comparator #(.width(3)) comparator_45 (.a(3'b111), .b(Instruction[14:12]), .eq(comparator_45_eq));  // open: gt, lt
  Comparator #(.width(3)) comparator_46 (.a(3'b100), .b(Instruction[14:12]), .eq(comparator_46_eq));  // open: gt, lt
  Comparator #(.width(3)) comparator_47 (.a(3'b110), .b(Instruction[14:12]), .eq(comparator_47_eq));  // open: gt, lt
  Comparator #(.width(3)) comparator_48 (.a(3'b001), .b(Instruction[14:12]), .eq(comparator_48_eq));  // open: gt, lt
  Priority_Encoder priority_encoder_1 (
    .in0(isBeq), .in1(isBge), .in2(isBgeu), .in3(isBlt), .in4(isBltu), .in5(isBne),
    .out(priority_encoder_1_out), .gs(priority_encoder_1_gs));  // open: in6, in7, en_in, en_out
  Priority_Encoder #(.select_enc(2)) priority_encoder_2 (
    .in0(isJ), .in1(isJr), .in2(isAuipc), .in3(isLui), .out(priority_encoder_2_out),
    .gs(priority_encoder_2_gs));  // open: en_out, en_in
  Priority_Encoder priority_encoder_3 (
    .in0(isLb), .in1(isLh), .in2(isLw), .in3(isSb), .in4(isSh), .in5(isSw), .out(priority_encoder_3_out),
    .gs(priority_encoder_3_gs));  // open: in6, in7, en_in, en_out
  not not_1 (not_1_out, BrEq);
  and and_22 (and_22_out, isBeq, BrEq);
  and and_23 (and_23_out, BrLt, isBlt);
  and and_24 (and_24_out, BrLt, isBltu);
  not not_2 (not_2_out, BrLt);
  not not_3 (not_3_out, BrLt);
  and and_25 (isBeq, isB, comparator_43_eq);
  and and_26 (isBge, isB, comparator_44_eq);
  and and_27 (isBgeu, isB, comparator_45_eq);
  and and_28 (isBlt, isB, comparator_46_eq);
  and and_29 (isBltu, isB, comparator_47_eq);
  and and_30 (isBne, isB, comparator_48_eq);
  Priority_Encoder priority_encoder_4 (
    .in0(isAddi), .in1(isAndi), .in2(isOri), .in3(isXori), .in4(isSlli), .in5(isSrli), .in6(isSrai),
    .in7(isSlti), .out(priority_encoder_4_out), .gs(priority_encoder_4_gs));  // open: en_in, en_out
  Priority_Encoder #(.select_enc(4)) priority_encoder_5 (
    .in0(isAdd), .in1(isSub), .in2(isAnd), .in3(isOr), .in4(isXor), .in5(isSll), .in10(isSrl), .in11(isSra),
    .in12(isSlt), .in13(isMul), .in14(isMulh), .in15(isMulhu), .out(priority_encoder_5_out),
    .gs(priority_encoder_5_gs));  // open: in6, in7, in8, in9, en_out, en_in
  Multiplexer #(.select(3), .width(6)) multiplexer_1 (
    .in0(6'b011010), .in1(6'b011101), .in2(6'b011111), .in3(6'b011100), .in4(6'b011110), .in5(6'b011011),
    .out(BAddr), .sel(priority_encoder_1_out));  // open: in6, in7
  Multiplexer #(.select(2), .width(6)) multiplexer_2 (
    .in0(6'b100010), .in1(6'b100011), .in2(6'b100000), .in3(6'b100001), .out(JUAddr),
    .sel(priority_encoder_2_out));
  Multiplexer #(.select(3), .width(6)) multiplexer_3 (
    .in0(6'b001100), .in1(6'b001101), .in2(6'b001110), .in3(6'b010111), .in4(6'b011000), .in5(6'b011001),
    .out(MemAddr), .sel(priority_encoder_3_out));  // open: in6, in7
  and and_31 (and_31_out, isBne, not_1_out);
  and and_32 (and_32_out, not_2_out, isBge);
  and and_33 (and_33_out, not_3_out, isBgeu);
  Multiplexer #(.select(3), .width(6)) multiplexer_4 (
    .in0(6'b001111), .in1(6'b010110), .in2(6'b010101), .in3(6'b010010), .in4(6'b010000), .in5(6'b010011),
    .in6(6'b010100), .in7(6'b010001), .out(IAddr), .sel(priority_encoder_4_out));
  Multiplexer #(.select(4), .width(6)) multiplexer_5 (
    .in0({6{1'b0}}), .in1(6'b000010), .in2(6'b001011), .in3(6'b001010), .in4(6'b000111), .in5(6'b000011),
    .in10(6'b001000), .in11(6'b001001), .in12(6'b000110), .in13(6'b000001), .in14(6'b000100),
    .in15(6'b000101), .out(RAddr), .sel(priority_encoder_5_out));  // open: in6, in7, in8, in9
  or or_1 (or_1_out, and_31_out, and_22_out, and_23_out, and_24_out, and_32_out, and_33_out);
  or or_2 (PCSel, isJ, isJr, or_1_out);
  Comparator #(.width(3)) comparator_49 (.a(3'b000), .b(Instruction[14:12]), .eq(comparator_49_eq));  // open: gt, lt
  Comparator #(.width(3)) comparator_50 (.a(3'b001), .b(Instruction[14:12]), .eq(comparator_50_eq));  // open: gt, lt
  Comparator #(.width(3)) comparator_51 (.a(3'b010), .b(Instruction[14:12]), .eq(comparator_51_eq));  // open: gt, lt
  Comparator #(.width(3)) comparator_52 (.a(3'b000), .b(Instruction[14:12]), .eq(comparator_52_eq));  // open: gt, lt
  Comparator #(.width(3)) comparator_53 (.a(3'b001), .b(Instruction[14:12]), .eq(comparator_53_eq));  // open: gt, lt
  Comparator #(.width(3)) comparator_54 (.a(3'b010), .b(Instruction[14:12]), .eq(comparator_54_eq));  // open: gt, lt
  and and_34 (isLb, isLd, comparator_49_eq);
  and and_35 (isLh, isLd, comparator_50_eq);
  and and_36 (isLw, isLd, comparator_51_eq);
  and and_37 (isSb, isS, comparator_52_eq);
  and and_38 (isSh, isS, comparator_53_eq);
  and and_39 (isSw, isS, comparator_54_eq);
  assign bit_extender_1_out = {{5{priority_encoder_4_gs}}, priority_encoder_4_gs};  // Bit_Extender bit_extender_1
  assign bit_extender_2_out = {{5{priority_encoder_5_gs}}, priority_encoder_5_gs};  // Bit_Extender bit_extender_2
  assign bit_extender_3_out = {{5{priority_encoder_1_gs}}, priority_encoder_1_gs};  // Bit_Extender bit_extender_3
  assign bit_extender_4_out = {{5{priority_encoder_2_gs}}, priority_encoder_2_gs};  // Bit_Extender bit_extender_4
  assign bit_extender_5_out = {{5{priority_encoder_3_gs}}, priority_encoder_3_gs};  // Bit_Extender bit_extender_5
  assign and_40_out = bit_extender_1_out & IAddr;  // AND_Gate and_40, 6 bits wide
  assign and_41_out = bit_extender_2_out & RAddr;  // AND_Gate and_41, 6 bits wide
  assign and_42_out = bit_extender_3_out & BAddr;  // AND_Gate and_42, 6 bits wide
  assign and_43_out = bit_extender_4_out & JUAddr;  // AND_Gate and_43, 6 bits wide
  assign and_44_out = bit_extender_5_out & MemAddr;  // AND_Gate and_44, 6 bits wide
  assign RomAddr = and_40_out | and_41_out | and_42_out | and_43_out | and_44_out;  // OR_Gate or_3, 6 bits wide

  // Other names for the same wires on the sheet: opcode[6:0] = Instruction[6:0]; rd[4:0] = Instruction[11:7];
  //   funct3[2:0] = Instruction[14:12]; rs1[4:0] = Instruction[19:15]; rs2[4:0] = Instruction[24:20];
  //   funct7[6:0] = Instruction[31:25]

  // Notes on the sheet:
  //   INPUTS to your circuit
  //   contents of rom_1 (hex, n*v repeats v):
  //   1001 1401 1601 1081 1481 1581 1101 1201 1281 1681 1301 1381 41 41 41 1041 10c1 1141 1241 12c1 16c1
  //   1341 13c1 1842 1842 1842 4*1064 1074 1074 1067 17e7 2069 2041
  //   ROM FOR CONTROL LOGIC
  //   DON'T CHANGE THE LOCATIONS OF THE INPUTS AND OUTPUTS!
  //   This is only if you choose to do the ROM option
  //   CONNECT
  //   WIRE
  //   TO
  //   USE
  //   ROM
  //   OUTPUT from your circuit
  //   Reminder: If using ROM, use combinational logic for PCSel
endmodule
