// Logisim project partial-load.circ as structural Verilog: 1 circuit, main circuit partial_load
module partial_load (
  input  [31:0] Instruction,
  input  [31:0] MemAddress,
  input  [31:0] DataFromMem,
  output [31:0] DataToReg
);

  wire and_1_out, and_2_out, and_3_out, comparator_1_eq, comparator_2_eq, comparator_2_gt, comparator_2_lt;
  wire [1:0] bitselector_1_out;
  wire [7:0] multiplexer_2_out;
  wire [15:0] multiplexer_1_out;
  wire [31:0] and_4_out, and_5_out, and_6_out, bit_extender_4_out, bit_extender_5_out, lb, lh, lw;

  Comparator #(.width(7)) comparator_1 (.a(7'b0000011), .b(Instruction[6:0]), .eq(comparator_1_eq));  // open: gt, lt
  Comparator #(.width(3)) comparator_2 (
    .a(Instruction[14:12]), .b(3'b001), .gt(comparator_2_gt), .eq(comparator_2_eq), .lt(comparator_2_lt));
  BitSelector #(.group(2), .width(32)) bitselector_1 (.in(MemAddress), .out(bitselector_1_out), .sel(4'b0000));
  and and_1 (and_1_out, comparator_1_eq, comparator_2_gt);
  and and_2 (and_2_out, comparator_1_eq, comparator_2_eq);
  and and_3 (and_3_out, comparator_1_eq, comparator_2_lt);
  assign lw = {{31{and_1_out}}, and_1_out};  // Bit_Extender bit_extender_1
  assign lh = {{31{and_2_out}}, and_2_out};  // Bit_Extender bit_extender_2
  assign lb = {{31{and_3_out}}, and_3_out};  // Bit_Extender bit_extender_3
  assign bit_extender_4_out = {{16{multiplexer_1_out[15]}}, multiplexer_1_out};  // Bit_Extender bit_extender_4
  Multiplexer #(.select(2), .width(16)) multiplexer_1 (
    .in0(DataFromMem[15:0]), .in1(DataFromMem[23:8]), .in2(DataFromMem[31:16]), .out(multiplexer_1_out),
    .sel(bitselector_1_out));  // open: in3
  assign bit_extender_5_out = {{24{multiplexer_2_out[7]}}, multiplexer_2_out};  // Bit_Extender bit_extender_5
  Multiplexer #(.select(2), .width(8)) multiplexer_2 (
    .in0(DataFromMem[7:0]), .in1(DataFromMem[15:8]), .in2(DataFromMem[23:16]), .in3(DataFromMem[31:24]),
    .out(multiplexer_2_out), .sel(bitselector_1_out));
  assign and_4_out = DataFromMem & lw;  // AND_Gate and_4, 32 bits wide
  assign and_5_out = bit_extender_4_out & lh;  // AND_Gate and_5, 32 bits wide
  assign and_6_out = bit_extender_5_out & lb;  // AND_Gate and_6, 32 bits wide
  assign DataToReg = and_4_out | and_5_out | and_6_out;  // OR_Gate or_1, 32 bits wide

  // Notes on the sheet:
  //   INPUTS to your circuit
  //   DON'T CHANGE THE LOCATIONS OF THE INPUTS AND OUTPUTS!
  //   OUTPUT from your circuit
endmodule
