// Logisim project partial-store.circ as structural Verilog: 1 circuit, main circuit partial_store
module partial_store (
  input  [31:0] Instruction,
  input  [31:0] MemAddress,
  input  [31:0] DataFromReg,
  input  MemWEn,
  output [3:0] MemWriteMask,
  output [31:0] DataToMem
);

  wire comparator_1_eq, comparator_2_eq, comparator_2_gt, comparator_2_lt, sb, sh, sw;
  wire [1:0] bitselector_1_out;
  wire [3:0] and_4_out, and_5_out, and_6_out, bit_extender_1_out, bit_extender_4_out, bit_extender_5_out,
       bit_extender_6_out, multiplexer_1_out, multiplexer_2_out;
  wire [7:0] bit_extender_3_out;
  wire [15:0] bit_extender_2_out;
  wire [31:0] and_7_out, and_8_out, and_9_out, bit_extender_7_out, bit_extender_8_out, bit_extender_9_out,
       multiplexer_3_out, multiplexer_4_out;

  BitSelector #(.group(2), .width(32)) bitselector_1 (.in(MemAddress), .out(bitselector_1_out), .sel(4'b0000));
  Comparator #(.width(7)) comparator_1 (.a(7'b0100011), .b(Instruction[6:0]), .eq(comparator_1_eq));  // open: gt, lt
  Comparator #(.width(3)) comparator_2 (
    .a(Instruction[14:12]), .b(3'b001), .gt(comparator_2_gt), .eq(comparator_2_eq), .lt(comparator_2_lt));
  assign bit_extender_1_out = {{3{MemWEn}}, MemWEn};  // Bit_Extender bit_extender_1
  Bit_Extender #(.in_width(32)) bit_extender_2 (.in(DataFromReg), .out(bit_extender_2_out));
  Bit_Extender #(.in_width(32), .out_width(8)) bit_extender_3 (.in(DataFromReg), .out(bit_extender_3_out));
  and and_1 (sw, comparator_1_eq, comparator_2_gt);
  and and_2 (sh, comparator_1_eq, comparator_2_eq);
  and and_3 (sb, comparator_1_eq, comparator_2_lt);
  assign bit_extender_4_out = {{3{sw}}, sw};  // Bit_Extender bit_extender_4
  assign bit_extender_5_out = {{3{sh}}, sh};  // Bit_Extender bit_extender_5
  Multiplexer #(.select(2), .width(4)) multiplexer_1 (
    .in0(4'b0011), .in2(4'b1100), .out(multiplexer_1_out), .sel(bitselector_1_out));  // open: in1, in3
  assign bit_extender_6_out = {{3{sb}}, sb};  // Bit_Extender bit_extender_6
  Multiplexer #(.select(2), .width(4)) multiplexer_2 (
    .in0(4'b0001), .in1(4'b0010), .in2(4'b0100), .in3(4'b1000), .out(multiplexer_2_out),
    .sel(bitselector_1_out));
  Multiplexer #(.select(2), .width(32)) multiplexer_3 (
    .in0({{16{1'b0}}, bit_extender_2_out}), .in2({bit_extender_2_out, {16{1'b0}}}), .out(multiplexer_3_out),
    .sel(bitselector_1_out));  // open: in1, in3
  Multiplexer #(.select(2), .width(32)) multiplexer_4 (
    .in0({{24{1'b0}}, bit_extender_3_out}), .in1({{16{1'b0}}, bit_extender_3_out, {8{1'b0}}}),
    .in2({{8{1'b0}}, bit_extender_3_out, {16{1'b0}}}), .in3({bit_extender_3_out, {24{1'b0}}}),
    .out(multiplexer_4_out), .sel(bitselector_1_out));
  assign and_4_out = bit_extender_4_out & bit_extender_1_out;  // AND_Gate and_4, 4 bits wide
  assign and_5_out = bit_extender_5_out & bit_extender_1_out & multiplexer_1_out;  // AND_Gate and_5, 4 bits wide
  assign and_6_out = bit_extender_6_out & bit_extender_1_out & multiplexer_2_out;  // AND_Gate and_6, 4 bits wide
  assign bit_extender_7_out = {{31{sw}}, sw};  // Bit_Extender bit_extender_7
  assign bit_extender_8_out = {{31{sh}}, sh};  // Bit_Extender bit_extender_8
  assign bit_extender_9_out = {{31{sb}}, sb};  // Bit_Extender bit_extender_9
  assign MemWriteMask = and_4_out | and_5_out | and_6_out;  // OR_Gate or_1, 4 bits wide
  assign and_7_out = DataFromReg & bit_extender_7_out;  // AND_Gate and_7, 32 bits wide
  assign and_8_out = multiplexer_3_out & bit_extender_8_out;  // AND_Gate and_8, 32 bits wide
  assign and_9_out = multiplexer_4_out & bit_extender_9_out;  // AND_Gate and_9, 32 bits wide
  assign DataToMem = and_7_out | and_8_out | and_9_out;  // OR_Gate or_2, 32 bits wide

  // Notes on the sheet:
  //   INPUTS to your circuit
  //   DON'T CHANGE THE LOCATIONS OF THE INPUTS AND OUTPUTS!
  //   OUTPUT from your circuit
endmodule
